# Fritzing sketch Schematic (saved by Fritzing 0.9.6b)

parts:
  Part1 = NeoPixel Stick [part_number=1426]
  JACK1 = 2.1mm Barrel Jack with Terminal Block
  WeMos_D1_Mini1 = WeMos D1 Mini

nets:
  +5V: Part1.+5V, JACK1.POS, WeMos_D1_Mini1.5V
  N1: Part1.GND, JACK1.NEG, WeMos_D1_Mini1.D1, WeMos_D1_Mini1.G
  N2: Part1.DATAIN, WeMos_D1_Mini1.D2

custom parts:
  NeoPixel Stick: Make your own little LED strip arrangement with this stick of NeoPixel LEDs. We crammed 8 of the tiny 5050 (5mm x 5mm) smart RGB LEDs onto a PCB with mounting holes and a chainable design. Use only one microcontroller pin to control as many as you can chain together! Each LED is addressable as the driver chip is inside the LED. Each one has ~18mA constant current drive so the color will be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
